// Logisim project ttt_wkt.circ as structural Verilog: 1 circuit, main circuit main
module main (
);

  wire b1, b2, b3, b4, b5, b6, b7, b8, b9, clock_1_out, clock_2_out, p1, p2, p3, p4, p5, p6, p7, p8, p9,
       Reset, Tie, Win;
  wire [7:0] rom_1_data;
  wire [8:0] demultiplexer_1_out1, Omoves;

  Clock clock_1 (.out(clock_1_out));
  J_K_Flip_Flop j_k_ff_1 (.J(p1), .clk(clock_1_out), .K(b1), .Q(Omoves[0]), .reset(Reset));  // open: Qn, preset, en
  J_K_Flip_Flop j_k_ff_2 (.J(p2), .clk(clock_1_out), .K(b2), .Q(Omoves[1]), .reset(Reset));  // open: Qn, preset, en
  J_K_Flip_Flop j_k_ff_3 (.J(p3), .clk(clock_1_out), .K(b3), .Q(Omoves[2]), .reset(Reset));  // open: Qn, preset, en
  J_K_Flip_Flop j_k_ff_4 (.J(p4), .clk(clock_1_out), .K(b4), .Q(Omoves[3]), .reset(Reset));  // open: Qn, preset, en
  J_K_Flip_Flop j_k_ff_5 (.J(p5), .clk(clock_1_out), .K(b5), .Q(Omoves[4]), .reset(Reset));  // open: Qn, preset, en
  J_K_Flip_Flop j_k_ff_6 (.J(p6), .clk(clock_1_out), .K(b6), .Q(Omoves[5]), .reset(Reset));  // open: Qn, preset, en
  J_K_Flip_Flop j_k_ff_7 (.J(p7), .clk(clock_1_out), .K(b7), .Q(Omoves[6]), .reset(Reset));  // open: Qn, preset, en
  J_K_Flip_Flop j_k_ff_8 (.J(p8), .clk(clock_1_out), .K(b8), .Q(Omoves[7]), .reset(Reset));  // open: Qn, preset, en
  J_K_Flip_Flop j_k_ff_9 (.J(p9), .clk(clock_1_out), .K(b9), .Q(Omoves[8]), .reset(Reset));  // open: Qn, preset, en
  ROM #(.addrWidth(18)) rom_1 (
    .addr({b9, b8, b7, b6, b5, b4, b3, b2, b1, Omoves}), .data({rom_1_data[7:6], Win, Tie, rom_1_data[3:0]}));  // open: sel
  Clock clock_2 (.out(clock_2_out));
  J_K_Flip_Flop j_k_ff_10 (
    .J(demultiplexer_1_out1[0]), .clk(clock_2_out), .K(1'b0), .Q(b1), .reset(Reset));  // open: Qn, preset, en
  J_K_Flip_Flop j_k_ff_11 (
    .J(demultiplexer_1_out1[1]), .clk(clock_2_out), .K(1'b0), .Q(b2), .reset(Reset));  // open: Qn, preset, en
  J_K_Flip_Flop j_k_ff_12 (
    .J(demultiplexer_1_out1[2]), .clk(clock_2_out), .K(1'b0), .Q(b3), .reset(Reset));  // open: Qn, preset, en
  J_K_Flip_Flop j_k_ff_13 (
    .J(demultiplexer_1_out1[3]), .clk(clock_2_out), .K(1'b0), .Q(b4), .reset(Reset));  // open: Qn, preset, en
  J_K_Flip_Flop j_k_ff_14 (
    .J(demultiplexer_1_out1[4]), .clk(clock_2_out), .K(1'b0), .Q(b5), .reset(Reset));  // open: Qn, preset, en
  J_K_Flip_Flop j_k_ff_15 (
    .J(demultiplexer_1_out1[5]), .clk(clock_2_out), .K(1'b0), .Q(b6), .reset(Reset));  // open: Qn, preset, en
  J_K_Flip_Flop j_k_ff_16 (
    .J(demultiplexer_1_out1[6]), .clk(clock_2_out), .K(1'b0), .Q(b7), .reset(Reset));  // open: Qn, preset, en
  J_K_Flip_Flop j_k_ff_17 (
    .J(demultiplexer_1_out1[7]), .clk(clock_2_out), .K(1'b0), .Q(b8), .reset(Reset));  // open: Qn, preset, en
  J_K_Flip_Flop j_k_ff_18 (
    .J(demultiplexer_1_out1[8]), .clk(clock_2_out), .K(1'b0), .Q(b9), .reset(Reset));  // open: Qn, preset, en
  Demultiplexer #(.select(4), .enable("false")) demultiplexer_1 (
    .out1(demultiplexer_1_out1[0]), .out2(demultiplexer_1_out1[1]), .out3(demultiplexer_1_out1[2]),
    .out4(demultiplexer_1_out1[3]), .out5(demultiplexer_1_out1[4]), .out6(demultiplexer_1_out1[5]),
    .out7(demultiplexer_1_out1[6]), .out8(demultiplexer_1_out1[7]), .out9(demultiplexer_1_out1[8]),
    .in(1'b1), .sel(rom_1_data[3:0]));  // open: out0, out10, out11, out12, out13, out14, out15
  Button button_1 (.out(p1));
  LED led_1 (.in(Omoves[0]));
  Button button_2 (.out(p4));
  LED led_2 (.in(Omoves[3]));
  LED led_3 (.in(Omoves[6]));
  Button button_3 (.out(p7));
  Button button_4 (.out(Reset));
  LED led_4 (.in(b1));
  Button button_5 (.out(p2));
  Button button_6 (.out(p5));
  LED led_5 (.in(b4));
  LED led_6 (.in(b7));
  Button button_7 (.out(p8));
  Button button_8 (.out(p3));
  LED led_7 (.in(b2));
  LED led_8 (.in(Omoves[1]));
  LED led_9 (.in(Omoves[4]));
  LED led_10 (.in(b5));
  Button button_9 (.out(p6));
  Button button_10 (.out(p9));
  LED led_11 (.in(b8));
  LED led_12 (.in(Omoves[7]));
  LED led_13 (.in(Tie));
  LED led_14 (.in(b3));
  LED led_15 (.in(Omoves[2]));
  LED led_16 (.in(b6));
  LED led_17 (.in(Omoves[5]));
  LED led_18 (.in(b9));
  LED led_19 (.in(Omoves[8]));
  LED led_20 (.in(Win));

  // Other names for the same wires on the sheet: u1 = Omoves[0]; u2 = Omoves[1]; u3 = Omoves[2]; u4 = Omoves[3];
  //   u5 = Omoves[4]; u6 = Omoves[5]; u7 = Omoves[6]; u8 = Omoves[7]; u9 = Omoves[8];
  //   Xmoves[8:0] = {b9, b8, b7, b6, b5, b4, b3, b2, b1}

  // Notes on the sheet:
  //   contents of rom_1 (hex, n*v repeats v):
  //   0 5 1 0 5 0 0 0 1 7*0 1 15*0 3 31*0 5 63*0 2 127*0 5 261*0 4 0 0 0 5 0 5 5*0 8 0 7 0 0 0 6 9*0 7 5*0
  //   5 7*0 4 17*0 5 5*0 2 7*0 3 49*0 5 5*0 3 7*0 2 113*0 5 5*0 3 7*0 3 368*0 7 0 0 7 0 0 0 7 7*0 1 15*0 7
  //   31*0 9 191*0 7 203*0 5 11*0 23 15*0 23 43*0 7 0 0 0 23 23*0 23 23*0 23 7*0 23 119*0 23 71*0 23 144*0
  //   4 4 5*0 5 7*0 4 47*0 1 63*0 1 127*0 1 305*0 8 5*0 22 9*0 5 5*0 22 7*0 22 25*0 5 13*0 22 9*0 5 5*0 22
  //   7*0 22 23*0 22 7*0 22 15*0 22 41*0 5 7*0 8 5*0 22 9*0 7 5*0 22 7*0 22 23*0 22 7*0 22 15*0 22 39*0 22
  //   7*0 22 15*0 22 695*0 20 15*0 20 7*0 20 39*0 20 15*0 20 7*0 20 23*0 20 7*0 20 15*0 20 55*0 20 15*0 20
  //   7*0 20 23*0 20 7*0 20 15*0 20 39*0 20 7*0 20 15*0 20 629*0 27 15*0 27 11*0 27 0 27 17*0 5 41*0 3
  //   21*0 5 41*0 2 85*0 6 41*0 3 899*0 27 59*0 23 191*0 23 114*0 5 13*0 9 8 46*0 5 5 13*0 1 48*0 5 5 13*0
  //   2 112*0 5 7 13*0 1 321*0 8 125*0 22 65*0 27 61*0 22 63*0 22 256*0 9 62*0 21 191*0 21 319*0 20 127*0
  //   20 63*0 20 82*0 3 0 2 1 0 0 7 0 0 1 20*0 2 0 0 9 28*0 4 1 0 2 0 0 0 1 23*0 2 32*0 4 0 0 4 59*0 9
  //   64*0 2 1 0 6 0 0 0 1 23*0 3 31*0 8 63*0 7 141*0 29 23*0 29 0 0 0 3 0 29 25*0 4 0 0 0 29 0 2 21*0 29
  //   5*0 2 29*0 4 0 0 0 3 0 29 21*0 3 5*0 2 25*0 29 5*0 29 61*0 6 0 0 0 3 0 6 21*0 3 5*0 3 25*0 8 5*0 8
  //   57*0 7 5*0 7 132*0 28 23*0 28 0 0 0 7 27*0 4 6*0 1 20*0 28 0 0 28 0 0 0 1 28*0 4 27*0 7 34*0 9 27*0
  //   9 36*0 6 0 0 0 7 23*0 3 31*0 28 0 0 28 27*0 28 32*0 7 234*0 28 63*0 29 31*0 29 27*0 23 99*0 28 27*0
  //   23 63*0 23 98*0 27 23*0 27 5*0 27 1 24*0 4 36*0 1 26*0 4 36*0 1 90*0 4 29*0 2 27 5*0 1 55*0 8 63*0
  //   27 201*0 29 63*0 27 31*0 29 23*0 29 5*0 22 65*0 27 31*0 8 23*0 8 5*0 22 33*0 27 23*0 27 5*0 22 384*0
  //   27 55*0 28 63*0 27 326*0 20 127*0 20 63*0 20 154*0 26 0 2 27*0 2 33*0 3 0 26 1 26*0 3 0 0 9 28*0 26
  //   0 0 26 124*0 26 63*0 26 0 0 26 225*0 29 63*0 27 31*0 26 127*0 26 63*0 26 222*0 28 63*0 9 31*0 26
  //   27*0 9 99*0 26 27*0 28 35*0 26 733*0 8 63*0 27 31*0 26 29*0 9 9 64*0 27 31*0 26 29*0 8 8 32*0 26
  //   29*0 27 27 2167*0 8 0 7 59*0 3 63*0 2 127*0 2 899*0 7 59*0 23 67*0 7 59*0 23 63*0 23 705*0 29 125*0
  //   22 127*0 22 895*0 20 127*0 20 63*0 20 893*0 27 47*0 25 63*0 25 3454*0 2 24 5*0 1 55*0 24 63*0 24
  //   393*0 7 55*0 24 5*0 8 57*0 24 5*0 7 384*0 28 55*0 24 63*0 24 2749*0 20 65*0 20 59*0 20 0 0 20 65*0
  //   20 58*0 20 0 0 20 60*0 20 0 0 20 321*0 20 127*0 20 63*0 20 318*0 20 127*0 20 63*0 20 829*0 20 127*0
  //   20 63*0 20 2194*0 24 5*0 6 9*0 24 0 0 0 5 7*0 24 0 24 95*0 24 13*0 24 113*0 24 13*0 3 354*0 5 0 0 0
  //   5 0 0 5 4*0 9 0 0 1 0 0 0 6 8*0 5 0 0 9 0 0 0 5 7*0 4 208*0 5 0 0 6 0 0 0 3 7*0 1 15*0 3 251*0 6
  //   23*0 24 223*0 24 0 0 0 23 23*0 23 889*0 25 7*0 24 111*0 24 486*0 25 14*0 21 8*0 25 6*0 21 7*0 21
  //   487*0 20 15*0 20 7*0 20 613*0 20 15*0 20 11*0 20 0 20 95*0 20 13*0 20 113*0 20 412*0 9 0 0 21 251*0
  //   21 259*0 20 223*0 20 27*0 20 370*0 25 14*0 21 111*0 21 399*0 20 111*0 20 1128*0 23 0 2 27*0 2 95*0
  //   23 127*0 2 119*0 23 1 0 6 0 0 0 23 23*0 23 141*0 29 123*0 23 127*0 23 91*0 24 0 0 0 23 0 6 21*0 23
  //   5*0 23 132*0 28 95*0 6 23*0 9 0 0 0 23 0 0 9 96*0 28 27*0 23 91*0 6 0 0 0 23 0 0 6 20*0 23 6*0 23
  //   610*0 20 23*0 20 5*0 20 95*0 20 152*0 20 94*0 20 6*0 20 23*0 20 265*0 20 127*0 20 95*0 20 23*0 20
  //   5*0 20 256*0 20 127*0 20 95*0 20 23*0 20 6*0 20 1277*0 20 223*0 20 1308*0 20 127*0 20 125*0 20 20
  //   2171*0 8 125*0 2 127*0 2 380*0 9 0 0 1 232*0 5 6*0 1 7*0 1 0 0 0 1 515*0 10 2937*0 20 3694*0 24 24
  //   5*0 1 513*0 10 510*0 10 3063*0 20 20 4239*0 7 0 0 0 6 23*0 4 31*0 3 191*0 3 1863*0 6 23*0 4 167*0 6
  //   23*0 4 31*0 4 1763*0 27 59*0 3 191*0 27 1280*0 9 62*0 1 191*0 1 575*0 10 1486*0 22 1 0 22 0 0 0 22
  //   23*0 22 485*0 6 0 0 0 3 0 22 21*0 3 5*0 22 164*0 20 23*0 20 59*0 20 0 0 20 220*0 20 0 0 20 0 0 0 20
  //   23*0 20 267*0 20 223*0 20 27*0 20 504*0 22 1 5*0 22 513*0 10 502*0 20 6*0 20 1788*0 20 251*0 20
  //   1025*0 10 2234*0 7 59*0 3 191*0 3 2111*0 10 6131*0 10 446*0 20 7440*0 29 23*0 24 223*0 24 3871*0 20
  //   223*0 20 27*0 20 4346*0 20 223*0 20 7696*0 10 16802*0 4 0 0 5 0 0 0 1 7*0 3 15*0 1 491*0 25 11*0 23
  //   11*0 25 0 0 0 23 7*0 23 1504*0 26 6*0 21 23*0 21 487*0 20 15*0 20 7*0 20 1492*0 5 11*0 3 15*0 3
  //   849*0 8 61*0 2 63*0 2 1087*0 10 81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
  //   Reset Button
endmodule
